# Fritzing sketch GambarRangkaian (saved by Fritzing 0.9.3b)

parts:
  U1 = ESP32-38PinWide [part_number=ESP32-38PinWide]
  Boost_Convertor1 = Boost Convertor [part_number=XL6009E1 package=THT]
  A1 = 2 channel relay module [package=THT]
  M1 = ac light dimmer-4terminal
  Part1 = LCD1602-I2C
  F2 = Fan - Ventilador [package=THT]
  Part2 = Lilypad Battery Connect
  J1 = Power Plug
  LED1 = LEDs [package=led10mm]
  Part3 = DHT22 module
  Fogger1 = Piezo Speaker

nets:
  N1: U1.GPIO12, A1.pin_15
  N2: U1.GND, A1.pin_14
  N3: U1.GPIO13, A1.pin_16
  N4: U1.VIN, A1.pin_13
  N5: U1.GPIO4, Part3.DATA
  N6: U1.GPIO18, M1.Z-C
  N7: U1.GPIO19, M1.PWM
  N8: U1.GPIO21, Part1.SDA
  N9: U1.GPIO22, Part1.SCL
  N10: Boost_Convertor1.Negative_Input, Fogger1.pin1
  N11: Boost_Convertor1.Positive_Input, A1.pin_5
  N12: Boost_Convertor1.Negative_Output, J1.GND, J1.tip_GND
  N13: Boost_Convertor1.Positive_Output, J1.PWR, J1.tip_PWR
  N14: A1.pin_1, F2.5V
  N15: A1.pin_4, Fogger1.pin2
  N16: M1.LOAD1, LED1.C
  N17: M1.LOAD2, LED1.A
  N18: M1.AC-IN1, Part2.-
  N19: M1.AC-IN2, Part2.+

notes:
  KIPAS DC 12V
  XL6009E1
  RELAY 2
  CHANNEL
  SENSOR DHT 22
  LCD I2C
  CATU DAYA 12V
  ESP 32
  MODUL AC LIGHT DIMMER
  220 VAC
  LAMPU PIJAR
  MIST MAKER

custom parts:
  ESP32-38PinWide: Generic 38-Pin ESP32 with wide format (only access to one side of pins on a breadboard) based on Stephen Lilley's HiLetgo ESP-WROOM-32 ESP32 ESP-32S Development Board.
  Boost Convertor: DC to DC boost convertor
  2 channel relay module: 2 channel Relay Module 5V 12V 24V High and Low Level Trigger Relay Control With Optocoupler Two Way relays DC 5 V 12 V 24 V Volt.
  ac light dimmer-4terminal: ac light dimmer module 4terminal.
  LCD1602-I2C: A standard character display, usually with 2x16 characters. Comes in many colors with LCM1602 IIC attached.
  Fan - Ventilador: Ventilador de 2 pines, se encuentra comunmente en computadoras de escritorio
  Power Plug: Power Jack This is the standard 5.5mm barrel plug for power. This part has bendable leads (i.e. wires in the real world) to connect to wall warts or the breadboard in the standard wire end, and hidden connectors on the tip end that will connect when "plugged in" (overlapped with the jack so it appears "plugged in" in breadboard) to the modified coax jack part. Internal busses connect the two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
  LEDs: LEDs Standard schematic elements and footprints for 5mm, 3mm, 1206, and 0603 sized LEDs. 5mm - Spark Fun Electronics SKU : COM-00529 (and others)
